# Fritzing sketch Stage01_TB_TL431 (saved by Fritzing 0.9.4)
breadboards: 1

parts:
  R1 = Resistor [tolerance=±5% resistance=5.6k package=THT]
  Part1 = Breadboard Power Supply Board SMD
  Q1 = TRANSISTOR_NPN [package=to-92]
  U1 = LM358 [package=dip08]
  R2 = Resistor [tolerance=±5% resistance=30.1k package=THT]
  R3 = Resistor [tolerance=±5% resistance=10k package=THT]
  R4 = Resistor [tolerance=±5% resistance=500 package=THT]
  Q2 = TRANSISTOR_PNP [package=to-92]

nets:
  N1: R1.Pin_0, U1.G$1_+IN
  N2: R1.Pin_1, Part1.VCC, Q1.A, U1.G$1_V+
  N3: Part1.GND, U1.G$1_V-, R2.Pin_1
  N4: U1.G$1_OUT, R4.Pin_1
  N5: U1.G$1_-IN, R2.Pin_0, R3.Pin_1
  N6: R3.Pin_0, Q2.C
  N7: R4.Pin_0, Q2.B

custom parts:
  TRANSISTOR_NPN: Generic NPN BJT. MMBT2222 is the common NPN we use. Double check against datasheet- not all devices are the same!
